// Logisim project shr79_lab4.circ as structural Verilog: 1 circuit, main circuit main
module main (
  input  [3:0] A,
  input  [3:0] B,
  input  sub
);

  wire adder_1_cout, or_1_out, SOV, undriven, UOV, xnor_1_out, xor_1_out, xor_2_out;
  wire [3:0] multiplexer_1_out, not_1_p2, not_2_p1, not_2_p2, not_3_out, O;

  // NOT_Gate #(.width(4)) not_1: pin names not known; wires that end beside it: B, not_1_p2
  Multiplexer #(.width(4)) multiplexer_1 (.in0(B), .in1(not_1_p2), .out(multiplexer_1_out), .sel(sub));  // open: en
  Adder #(.width(4)) adder_1 (.a(A), .b(multiplexer_1_out), .out(O), .cin(sub), .cout(adder_1_cout));
  // Probe on A
  // Probe on B
  // Probe on O
  // Probe on A
  // Probe on B
  // Probe on O
  LED led_1 (.in(UOV));
  // NOT_Gate #(.width(4)) not_2: pin names not known; wires that end beside it: not_2_p1, not_2_p2
  Multiplexer #(.width(4)) multiplexer_2 (.in0(not_3_out), .in1(B), .out(not_2_p2), .sel(sub));  // open: en
  assign not_3_out = ~B;  // NOT_Gate not_3, 4 bits wide
  // Probe on A
  // Probe on B
  // Probe on O
  xnor xnor_1 (xnor_1_out, A[3], not_2_p1[3]);
  ExactlyOne xor_1 (.out(xor_1_out), .in1(A[3]), .in3(O[3]), .in4(undriven));
  ExactlyOne xor_2 (.out(xor_2_out), .in0(undriven), .in1(not_2_p1[3]), .in3(O[3]));
  // XOR_Gate xor_3: pin names not known; wires that end beside it: sub, adder_1_cout, UOV
  or or_1 (or_1_out, xor_1_out, xor_2_out);
  and and_1 (SOV, xnor_1_out, or_1_out);
  // Probe on A
  // Probe on B
  // Probe on O
  LED led_2 (.in(SOV));
endmodule
