// Logisim project shr79_lab5.circ as structural Verilog: 2 circuits, main circuit main
module main (
  input  [3:0] A,
  input  [3:0] B
);

  wire button_1_out, CLK, clock_1_out, not_1_p1, not_1_p2, not_2_p2;
  wire [7:0] adder_1_out, adder_2_out, adder_3_out, partial_prod_1_out_4, partial_prod_2_out_4,
       partial_prod_3_out_4, partial_prod_4_out_4;
  wire [15:0] bit_extender_1_out, Dividend_Rem_q, Divisor_q, or_2_out, Quotient_q, shifter_1_out,
       shifter_2_out, subtractor_1_out;

  // Probe on A
  // Probe on B
  Clock clock_1 (.out(clock_1_out));
  or or_1 (CLK, clock_1_out, button_1_out);
  Button button_1 (.out(button_1_out));
  Register #(.width(16)) Dividend_Rem (
    .D(subtractor_1_out), .en(not_1_p1), .Q(Dividend_Rem_q), .clk(CLK));  // open: clr
  // Probe on partial_prod_1_out_4
  partial_prod partial_prod_1 (.A(A), .shift(3'b011), .B(B[3]), .out_4(partial_prod_1_out_4));
  // Probe on partial_prod_2_out_4
  partial_prod partial_prod_2 (.A(A), .shift(3'b010), .B(B[2]), .out_4(partial_prod_2_out_4));
  // Probe on partial_prod_3_out_4
  partial_prod partial_prod_3 (.A(A), .shift(3'b001), .B(B[1]), .out_4(partial_prod_3_out_4));
  // Probe on partial_prod_4_out_4
  partial_prod partial_prod_4 (.A(A), .shift(3'b000), .B(B[0]), .out_4(partial_prod_4_out_4));
  Register #(.width(16)) Divisor (.D(shifter_1_out), .Q(Divisor_q), .clk(CLK));  // open: en, clr
  // NOT_Gate not_1: pin names not known; wires that end beside it: not_1_p1, not_1_p2
  Adder adder_1 (.a(partial_prod_1_out_4), .b(partial_prod_2_out_4), .out(adder_1_out));  // open: cin, cout
  Adder adder_2 (.a(partial_prod_3_out_4), .b(partial_prod_4_out_4), .out(adder_2_out));  // open: cin, cout
  // Probe on Divisor_q
  // Probe on Quotient_q
  Register #(.width(16)) Quotient (.D(or_2_out), .Q(Quotient_q), .clk(CLK));  // open: en, clr
  Adder adder_3 (.a(adder_1_out), .b(adder_2_out), .out(adder_3_out));  // open: cin, cout
  // Probe on adder_3_out
  Shifter #(.width(16), .shift("lr")) shifter_1 (.in(Divisor_q), .\dist (4'b0001), .out(shifter_1_out));
  // Probe on shifter_1_out
  // Probe on Dividend_Rem_q
  // Probe on subtractor_1_out
  Subtractor #(.width(16)) subtractor_1 (
    .a(Dividend_Rem_q), .b(Divisor_q), .out(subtractor_1_out), .bout(not_1_p2));  // open: bin
  // NOT_Gate not_2: pin names not known; wires that end beside it: not_1_p2, not_2_p2
  assign bit_extender_1_out = {{15{1'b0}}, not_2_p2};  // Bit_Extender bit_extender_1
  Shifter #(.width(16)) shifter_2 (.in(Quotient_q), .\dist (4'b0001), .out(shifter_2_out));
  assign or_2_out = bit_extender_1_out | shifter_2_out;  // OR_Gate or_2, 16 bits wide

  // Notes on the sheet:
  //   partial products
  //   Look inside these components -
  //   they compute the partial products.
  //   tree o' adders
endmodule

module partial_prod (
  input  [3:0] A,
  input  [2:0] shift,
  input  B,
  output [7:0] out_4
);

  wire [3:0] multiplexer_1_out;
  wire [7:0] bit_extender_1_out;

  assign bit_extender_1_out = {{4{1'b0}}, multiplexer_1_out};  // Bit_Extender bit_extender_1
  Multiplexer #(.width(4)) multiplexer_1 (.in0(4'b0000), .in1(A), .out(multiplexer_1_out), .sel(B));  // open: en
  Shifter shifter_1 (.in(bit_extender_1_out), .\dist (shift), .out(out_4));

  // Notes on the sheet:
  //   this makes the 4-bit input into an 8-bit number.
  //   this left-shifts to the correct position.
endmodule
